# Fritzing sketch Relay (saved by Fritzing 0.9.3b)
breadboards: 1

parts:
  Netduino1 = Netduino Plus2
  U1 = RELAY [package=relay-g5q]
  LED1 = LED - 5mm [color="Red (633nm)" package="5 mm [THT]"]
  R1 = Resistor [tolerance=±5% resistance=100 package=THT]
  R2 = Resistor [tolerance=±5% resistance=100 package=THT]
  LED2 = LED - 5mm [color="Green (565nm)" package="5 mm [THT]"]

nets:
  N1: Netduino1.GND, U1.COIL1, R1.Pin_0, R2.Pin_0
  N2: Netduino1.D2_RX1, U1.COIL2
  N3: Netduino1.3V3, U1.MAIN
  N4: U1.NO, LED2.anode
  N5: U1.NC, LED1.anode
  N6: LED1.cathode, R1.Pin_1
  N7: R2.Pin_1, LED2.cathode
