# Fritzing sketch Level_Shifting_Lab (saved by Fritzing 0.9.3b)
breadboards: 1

parts:
  5V_Light_Sensor = LilyPad Light Sensor
  Netduino = Netduino Plus2
  R1 = Resistor [tolerance=±5% resistance=11k package=THT]
  R2 = Resistor [tolerance=±5% resistance=2.2k package=THT]

nets:
  N1: 5V_Light_Sensor.+, Netduino.+5V
  N2: 5V_Light_Sensor.-, Netduino.GND, R2.Pin_1
  N3: 5V_Light_Sensor.S, R1.Pin_0
  N4: Netduino.A2, R1.Pin_1, R2.Pin_0
