# Fritzing sketch SevenSegment (saved by Fritzing 0.9.3b)

parts:
  Meadow1 = Meadow F7 Micro
  U1 = 7-SEGMENT-DISPLAY [package=7-segment-display]

nets:
  N1: Meadow1.GND, Meadow1.D13, U1.F, U1.G
  N2: Meadow1.D12, U1.E
  N3: Meadow1.SCK/D08, U1.D
  N4: Meadow1.SDA/D07, U1.G1
  N5: Meadow1.D06, U1.DP
  N6: Meadow1.D05, U1.B
  N7: Meadow1.D14, U1.G2
  N8: Meadow1.D15, U1.A

custom parts:
  Meadow F7 Micro: A prototyping board running full .Net Standard 2.X
