# Fritzing sketch SerialLCD (saved by Fritzing 0.9.3b)
breadboards: 1

parts:
  Meadow1 = Meadow F7
  U2 = LCD-16X2 [package=lcd-16x2_noholes]  # not connected
  R1 = Resistor [tolerance=±5% resistance=220 package=THT]
  R2 = Resistor [tolerance=±5% resistance=220 package=THT]
  R3 = Resistor [tolerance=±5% resistance=220 package=THT]

nets:
  N1: Meadow1.GND, R3.Pin_0
  N2: Meadow1.D12, R2.Pin_0
  N3: Meadow1.3V3, R1.Pin_0

custom parts:
  Meadow F7: A prototyping board running full .Net Standard 2.X
