# Fritzing sketch MCP23008 (saved by Fritzing 0.9.3b)
breadboards: 1

parts:
  R1 = Resistor [tolerance=±5% resistance=220 package=THT]
  R2 = Resistor [tolerance=±5% resistance=220 package=THT]
  R3 = Resistor [tolerance=±5% resistance=220 package=THT]
  R4 = Resistor [tolerance=±5% resistance=220 package=THT]
  R5 = Resistor [tolerance=±5% resistance=220 package=THT]
  R6 = Resistor [tolerance=±5% resistance=220 package=THT]
  R7 = Resistor [tolerance=±5% resistance=220 package=THT]
  R8 = Resistor [tolerance=±5% resistance=220 package=THT]
  LED2 = LED - 5mm [color="Red (633nm)" package="5 mm [THT]"]
  LED3 = LED - 5mm [color="Red (633nm)" package="5 mm [THT]"]
  LED4 = LED - 5mm [color="Red (633nm)" package="5 mm [THT]"]
  LED5 = LED - 5mm [color="Red (633nm)" package="5 mm [THT]"]
  LED6 = LED - 5mm [color="Red (633nm)" package="5 mm [THT]"]
  LED7 = LED - 5mm [color="Red (633nm)" package="5 mm [THT]"]
  LED8 = LED - 5mm [color="Red (633nm)" package="5 mm [THT]"]
  LED9 = LED - 5mm [color="Red (633nm)" package="5 mm [THT]"]
  R9 = Resistor [tolerance=±5% resistance=4.1k package=THT]
  R10 = Resistor [tolerance=±5% resistance=4.1k package=THT]
  IC5 = FRM010 [package=THT]
  Meadow1 = Meadow F7

nets:
  N1: R1.Pin_0, R2.Pin_0, R3.Pin_0, R4.Pin_0, R5.Pin_0, R6.Pin_0, R7.Pin_0, R8.Pin_0, IC5.LCD_D7, Meadow1.GND
  N2: R1.Pin_1, LED9.cathode
  N3: R2.Pin_1, LED3.cathode
  N4: R3.Pin_1, LED4.cathode
  N5: R4.Pin_1, LED5.cathode
  N6: R5.Pin_1, LED2.cathode
  N7: R6.Pin_1, LED6.cathode
  N8: R7.Pin_1, LED7.cathode
  N9: R8.Pin_1, LED8.cathode
  N10: LED2.anode, IC5.LED
  N11: LED3.anode, IC5.XTAL#15
  N12: LED4.anode, IC5.XTAL#14
  N13: LED5.anode, IC5.+V
  N14: LED6.anode, IC5.JP4_-_Number_of_Lines_selection
  N15: LED7.anode, IC5.JP3_-_Polarity_selection
  N16: LED8.anode, IC5.JP2_-_Baud_Rate_selection
  N17: LED9.anode, IC5.JP1_-_Welcome_Message_selection
  N18: R9.Pin_0, R10.Pin_0, IC5.Serial_In, IC5.Reset, IC5.0V, IC5.LCD_D4, IC5.LCD_PWR, Meadow1.3V3
  N19: R9.Pin_1, IC5.LCD_RS, Meadow1.SCK/D08
  N20: R10.Pin_1, IC5.LCD_E, Meadow1.SDA/D07

custom parts:
  Meadow F7: A prototyping board running full .Net Standard 2.X
