# Fritzing sketch x74595 (saved by Fritzing 0.9.3b)
breadboards: 1

parts:
  U1 = 74HC595 [package="DIP16 [THT]"]
  LED1 = LED - 3mm [color="Red (633nm)" package="3 mm [THT]"]
  LED2 = LED - 3mm [color="Red (633nm)" package="3 mm [THT]"]
  LED3 = LED - 3mm [color="Red (633nm)" package="3 mm [THT]"]
  LED4 = LED - 3mm [color="Red (633nm)" package="3 mm [THT]"]
  LED5 = LED - 3mm [color="Red (633nm)" package="3 mm [THT]"]
  LED6 = LED - 3mm [color="Red (633nm)" package="3 mm [THT]"]
  LED7 = LED - 3mm [color="Red (633nm)" package="3 mm [THT]"]
  R1 = Resistor [tolerance=±5% resistance=220 package=THT]
  R2 = Resistor [tolerance=±5% resistance=220 package=THT]
  R3 = Resistor [tolerance=±5% resistance=220 package=THT]
  R4 = Resistor [tolerance=±5% resistance=220 package=THT]
  R5 = Resistor [tolerance=±5% resistance=220 package=THT]
  R6 = Resistor [tolerance=±5% resistance=220 package=THT]
  R7 = Resistor [tolerance=±5% resistance=220 package=THT]
  LED8 = LED - 3mm [color="Red (633nm)" package="3 mm [THT]"]
  R8 = Resistor [tolerance=±5% resistance=220 package=THT]
  Meadow1 = Meadow F7

nets:
  N1: U1.Q1, R2.Pin_0
  N2: U1.Q2, R3.Pin_0
  N3: U1.Q3, R4.Pin_0
  N4: U1.Q4, R5.Pin_0
  N5: U1.Q5, R6.Pin_0
  N6: U1.Q6, R7.Pin_0
  N7: U1.Q7, R1.Pin_0
  GND: U1.GND, U1.OE, LED1.cathode, LED2.cathode, LED3.cathode, LED4.cathode, LED5.cathode, LED6.cathode, LED7.cathode, LED8.cathode, Meadow1.GND
  VCC: U1.MR, U1.VCC, Meadow1.3V3
  N8: U1.SH_CP, Meadow1.SCK
  N9: U1.ST_CP, Meadow1.D09
  N10: U1.DS, Meadow1.MOSI
  N11: U1.Q0, R8.Pin_0
  N12: LED1.anode, R5.Pin_1
  N13: LED2.anode, R7.Pin_1
  N14: LED3.anode, R4.Pin_1
  N15: LED4.anode, R1.Pin_1
  N16: LED5.anode, R3.Pin_1
  N17: LED6.anode, R2.Pin_1
  N18: LED7.anode, R8.Pin_1
  N19: R6.Pin_1, LED8.anode

custom parts:
  Meadow F7: A prototyping board running full .Net Standard 2.X
