# Fritzing sketch x74595_Fritzing (saved by Fritzing 0.9.3b)
breadboards: 1

parts:
  U1 = 74HC595 [package="DIP16 [THT]"]
  LED7 = LED - 3mm [color="Red (633nm)" package="3 mm [THT]"]
  R1 = Resistor [tolerance=±5% resistance=220 package=THT]
  R2 = Resistor [tolerance=±5% resistance=220 package=THT]
  R3 = Resistor [tolerance=±5% resistance=220 package=THT]
  R4 = Resistor [tolerance=±5% resistance=220 package=THT]
  R5 = Resistor [tolerance=±5% resistance=220 package=THT]
  R6 = Resistor [tolerance=±5% resistance=220 package=THT]
  R7 = Resistor [tolerance=±5% resistance=220 package=THT]
  R8 = Resistor [tolerance=±5% resistance=220 package=THT]
  Meadow1 = Meadow F7
  LED9 = LED - 3mm [color="Red (633nm)" package="3 mm [THT]"]
  LED10 = LED - 3mm [color="Red (633nm)" package="3 mm [THT]"]
  LED11 = LED - 3mm [color="Red (633nm)" package="3 mm [THT]"]
  LED12 = LED - 3mm [color="Red (633nm)" package="3 mm [THT]"]
  LED13 = LED - 3mm [color="Red (633nm)" package="3 mm [THT]"]
  LED14 = LED - 3mm [color="Red (633nm)" package="3 mm [THT]"]
  LED15 = LED - 3mm [color="Red (633nm)" package="3 mm [THT]"]

nets:
  N1: U1.Q1, LED15.anode
  N2: U1.Q2, LED14.anode
  N3: U1.Q3, LED12.anode
  N4: U1.Q4, LED11.anode
  N5: U1.Q5, LED10.anode
  N6: U1.Q6, LED9.anode
  N7: U1.Q7, LED7.anode
  GND: U1.GND, U1.OE, R1.Pin_1, R2.Pin_1, R3.Pin_1, R4.Pin_1, R5.Pin_1, R6.Pin_1, R7.Pin_1, R8.Pin_1, Meadow1.GND
  VCC: U1.MR, U1.VCC, Meadow1.3V3
  N8: U1.SH_CP, Meadow1.SCK
  N9: U1.ST_CP, Meadow1.D03
  N10: U1.DS, Meadow1.MOSI
  N11: U1.Q0, LED13.anode
  N12: LED7.cathode, R1.Pin_0
  N13: R2.Pin_0, LED15.cathode
  N14: R3.Pin_0, LED14.cathode
  N15: R4.Pin_0, LED12.cathode
  N16: R5.Pin_0, LED11.cathode
  N17: R6.Pin_0, LED10.cathode
  N18: R7.Pin_0, LED9.cathode
  N19: R8.Pin_0, LED13.cathode

custom parts:
  Meadow F7: A prototyping board running full .Net Standard 2.X
