# Fritzing sketch LedBarGraph (saved by Fritzing 0.9.3b)
breadboards: 1

parts:
  Meadow1 = Meadow F7
  R4 = Resistor [tolerance=±5% resistance=220 package=THT]
  R5 = Resistor [tolerance=±5% resistance=220 package=THT]
  R6 = Resistor [tolerance=±5% resistance=220 package=THT]
  R7 = Resistor [tolerance=±5% resistance=220 package=THT]
  R8 = Resistor [tolerance=±5% resistance=220 package=THT]
  R9 = Resistor [tolerance=±5% resistance=220 package=THT]
  R10 = Resistor [tolerance=±5% resistance=220 package=THT]
  R11 = Resistor [tolerance=±5% resistance=220 package=THT]
  R12 = Resistor [tolerance=±5% resistance=220 package=THT]
  R13 = Resistor [tolerance=±5% resistance=220 package=THT]

nets:
  N1: Meadow1.D13, R5.Pin_0
  N2: Meadow1.D12, R4.Pin_0
  N3: Meadow1.D11, R10.Pin_0
  N4: Meadow1.D10, R8.Pin_0
  N5: Meadow1.D09, R9.Pin_0
  N6: Meadow1.SCK/D08, R11.Pin_0
  N7: Meadow1.SDA/D07, R12.Pin_0
  N8: Meadow1.D06, R13.Pin_0
  N9: Meadow1.D14, R6.Pin_0
  N10: Meadow1.D15, R7.Pin_0

custom parts:
  Meadow F7: A prototyping board running full .Net Standard 2.X
