# Fritzing sketch PwmLed (saved by Fritzing 0.9.3b)
breadboards: 1

parts:
  LED4 = LED - 3mm [color="Red (633nm)" package="3 mm [THT]"]
  Meadow1 = Meadow F7

nets:
  N1: LED4.cathode, Meadow1.GND
  N2: LED4.anode, Meadow1.SCK/D08

custom parts:
  Meadow F7: A prototyping board running full .Net Standard 2.X
