# Fritzing sketch RgbPwmLed (saved by Fritzing 0.9.3b)
breadboards: 1

parts:
  Meadow1 = Meadow F7
  LED5 = RGB LED (com. cathode, rgb) [package="5 mm [THT]"]

nets:
  N1: Meadow1.GND, LED5.common_cathode
  N2: Meadow1.D11, LED5.red_anode
  N3: Meadow1.D10, LED5.green_anode
  N4: Meadow1.D09, LED5.blue_anode

custom parts:
  Meadow F7: A prototyping board running full .Net Standard 2.X
