# Fritzing sketch BMP085 (saved by Fritzing 0.9.3b)
breadboards: 1

parts:
  Part2 = Barometric Pressure Sensor - BMP085 Breakout
  Meadow1 = Meadow F7

nets:
  VCC: Part2.VCC, Meadow1.3V3
  GND: Part2.GND, Meadow1.GND

custom parts:
  Meadow F7: A prototyping board running full .Net Standard 2.X
