# Fritzing sketch SHT31D_Fritzing (saved by Fritzing 0.9.3b)
breadboards: 1

parts:
  Meadow1 = Meadow F7
  Part1 = Adafruit SHT31-D Sensirion Temperature/Humidity Sensor [part_number="Adafruit #2857"]

nets:
  GND: Meadow1.GND, Part1.GND, Part1.ADDR
  N1: Meadow1.SCK/D08, Part1.SCL
  N2: Meadow1.SDA/D07, Part1.SDA
  3V3: Meadow1.3V3, Part1.VIN

custom parts:
  Meadow F7: A prototyping board running full .Net Standard 2.X
  Adafruit SHT31-D Sensirion Temperature/Humidity Sensor: Sensirion Temperature/Humidity sensors are some of the finest & highest-accuracy devices you can get. And, finally we have some that have a true I2C interface for easy reading. The SHT31-D sensor has an excellent ±2% relative humidity and ±0.3°C accuracy for most uses. Unlike earlier SHT sensors, this sensor has a true I2C interface, and (bonus!) even with two address options. It also is 3V or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
