# Fritzing sketch SI7021 (saved by Fritzing 0.9.3b)
breadboards: 1

parts:
  Meadow1 = Meadow F7
  Part2 = Adafruit Si7021 Temp Humidity [part_number="Adafruit #3251"]

nets:
  GND: Meadow1.GND, Part2.GND
  N1: Meadow1.SCK/D08, Part2.SCL
  N2: Meadow1.SDA/D07, Part2.SDA
  3V3: Meadow1.3V3, Part2.VIN

custom parts:
  Meadow F7: A prototyping board running full .Net Standard 2.X
  Adafruit Si7021 Temp Humidity: It's summer and you're sweating and your hair's all frizzy and all you really want to know is why the weatherman said this morning that today's relative humidity would max out at a perfectly reasonable 42% when it feels more like 77%. Enter the Si7021 Temperature + Humidity Sensor - the best way to prove the weatherman wrong! This lovely sensor for Silicon labs has ± 3% relative humidity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
