# Fritzing sketch PushButton (saved by Fritzing 0.9.3b)
breadboards: 1

parts:
  Meadow1 = Meadow F7
  S1 = Pushbutton [package="[THT]"]

nets:
  N1: Meadow1.GND, S1.Pin_1, S1.Pin_2
  N2: Meadow1.SCK/D08, S1.Pin_3, S1.Pin_4

custom parts:
  Meadow F7: A prototyping board running full .Net Standard 2.X
