# Fritzing sketch LinearHallEffectTachometer (saved by Fritzing 0.9.3b)
breadboards: 1

parts:
  Meadow1 = Meadow F7
  Q1 = NPN-Transistor [package="TO92 [THT]"]

nets:
  N1: Meadow1.GND, Q1.B
  N2: Meadow1.D10, Q1.E
  N3: Meadow1.+5V, Q1.C

custom parts:
  Meadow F7: A prototyping board running full .Net Standard 2.X
