# Fritzing sketch ALSPT19315C (saved by Fritzing 0.9.3b)
breadboards: 1

parts:
  Meadow1 = Meadow F7
  Part2 = ALSPT19315C

nets:
  GND: Meadow1.GND, Part2.GND
  3V3: Meadow1.3V3, Part2.VCC
  N1: Meadow1.A3, Part2.OUT

custom parts:
  Meadow F7: A prototyping board running full .Net Standard 2.X
  ALSPT19315C: Add a teeny analog light sensor, the ALS PT19 analog light sensor is a great way to upgrade a project that uses a photocell and needs RoHS compliance. Due to the high rejection ratio of infrared radiation, the spectral response of the ambient light sensor is close to that of human eyes. It's a pretty simple sensor - connect - to ground, + to 2.5V-5.5V or so to power it. Now measure the analog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
