# Fritzing sketch SI1145 (saved by Fritzing 0.9.3b)
breadboards: 1

parts:
  Part2 = SI1145 Digital UV Index + IR + Visible Light Sensor [part_number=1777]
  Meadow1 = Meadow F7

nets:
  +5V: Part2.+5V, Meadow1.3V3
  GND: Part2.GND, Meadow1.GND
  N1: Part2.SCL, Meadow1.SDA/D07
  N2: Part2.SDA, Meadow1.SCK/D08

custom parts:
  SI1145 Digital UV Index + IR + Visible Light Sensor: The SI1145 is a new sensor from SiLabs with a calibrated light sensing algorithm that can calculate UV Index. It doesn't contain an actual UV sensing element, instead it approximates it based on visible & IR light from the sun. We took this outside a couple days and compared the calculated UV index with the news-reported index and found it was very accurate! It's a digital sensor that works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
  Meadow F7: A prototyping board running full .Net Standard 2.X
