# Fritzing sketch TSL2561 (saved by Fritzing 0.9.3b)
breadboards: 1

parts:
  Part2 = Adafruit TSL2591 [part_number="Adafruit #1980"]
  Meadow1 = Meadow F7

nets:
  VIN: Part2.VIN, Meadow1.3V3
  GND: Part2.GND, Meadow1.GND
  N1: Part2.INT, Meadow1.D09
  N2: Part2.SDA, Meadow1.SDA/D07
  N3: Part2.SCL, Meadow1.SCK/D08

custom parts:
  Adafruit TSL2591: When the future is dazzlingly-bright, this ultra-high-range luminosity sensor will help you measure it. The TSL2591 luminosity sensor is an advanced digital light sensor, ideal for use in a wide range of light situations. Compared to low cost CdS cells, this sensor is more precise, allowing for exact lux calculations and can be configured for different gain/timing ranges to detect light ranges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
  Meadow F7: A prototyping board running full .Net Standard 2.X
