# Fritzing sketch Capacitive (saved by Fritzing 0.9.3b)
breadboards: 1

parts:
  Meadow1 = Meadow F7
  Q1 = PNP-Transistor [package="TO92 [THT]"]

nets:
  N1: Meadow1.GND, Q1.C
  N2: Meadow1.3V3, Q1.B
  N3: Meadow1.A0, Q1.E

custom parts:
  Meadow F7: A prototyping board running full .Net Standard 2.X
