# Fritzing sketch Adx337 (saved by Fritzing 0.9.3b)
breadboards: 1

parts:
  Meadow1 = Meadow F7
  Part2 = Triple Axis Accelerometer Breakout - ADXL335

nets:
  GND: Meadow1.GND, Part2.ST, Part2.GND
  3V3: Meadow1.3V3, Part2.VCC
  N1: Meadow1.A0, Part2.ZOUT
  N2: Meadow1.A1, Part2.YOUT
  N3: Meadow1.A2, Part2.XOUT

custom parts:
  Meadow F7: A prototyping board running full .Net Standard 2.X
