# Fritzing sketch Bno055 (saved by Fritzing 0.9.3b)
breadboards: 1

parts:
  Meadow1 = Meadow F7
  Part2 = 9-DOF Absolute Orientation IMU Fusion Breakout - BNO055

nets:
  GND: Meadow1.GND, Part2.GND
  N1: Meadow1.SCK/D08, Part2.SCL_5V
  N2: Meadow1.SDA/D07, Part2.SDA_5V
  N3: Meadow1.D06, Part2.RST_5V
  N4: Meadow1.3V3, Part2.5.0V

custom parts:
  Meadow F7: A prototyping board running full .Net Standard 2.X
  9-DOF Absolute Orientation IMU Fusion Breakout - BNO055: A MEMS accelerometer, magnetometer and gyroscope on a single die with a high speed ARM Cortex-M0 based processor to digest all the sensor data, abstract the sensor fusion and real time requirements away, and spit out data you can use in quaternions, Euler angles or vectors.
