# Fritzing sketch IDxxLA-RFID Reader Breakout (saved by Fritzing 0.9.4)
breadboards: 1

parts:
  Mod1 = Meadow F7 Micro
  Part1 = RFID_Breakout_v2
  LED1 = LED - 5mm [color="Green (565nm)" package="5 mm [THT]"]
  R1 = Resistor [tolerance=±5% resistance=330 package=THT]

nets:
  GND: Mod1.GND, Part1.FORM, Part1.GND, LED1.cathode
  N1: Mod1.D13, Part1.D0
  +5V: Mod1.+5V, Part1.VCC
  N2: Part1.READ, R1.Pin_1
  N3: LED1.anode, R1.Pin_0

custom parts:
  RFID_Breakout_v2: This is a simple breakout board for our RFID readers. The SparkFun RFID Reader Breakout converts the 2mm pins to bread board friendly 0.1" headers. With this ability the ID-3LA, ID-12LA, and the ID-20LA you can solder the reader directly to the breakout board or use the 2mm sockets. This breakout board’s edges actually fit flush within the under side the ID-12LA. The board also works with the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
