# Fritzing sketch RotaryEncoder (saved by Fritzing 0.9.3b)
breadboards: 1

parts:
  Meadow1 = Meadow F7
  RE1 = Rotary Encoder [package=THT]
  LED1 = LED - 5mm [color="Red (633nm)" package="5 mm [THT]"]

nets:
  N1: Meadow1.GND, LED1.cathode
  N2: Meadow1.D12, LED1.anode
  N3: Meadow1.D09, RE1.EncoderPinA
  N4: Meadow1.SDA/D07, RE1.EncoderPinB
  N5: Meadow1.3V3, RE1.EncoderPinC

custom parts:
  Meadow F7: A prototyping board running full .Net Standard 2.X
