# Fritzing sketch SpstSwitch (saved by Fritzing 0.9.3b)
breadboards: 1

parts:
  Meadow1 = Meadow F7
  S2 = Toggle Switch spst [package=THT]

nets:
  N1: Meadow1.D13, S2.L1
  N2: Meadow1.3V3, S2.COM

custom parts:
  Meadow F7: A prototyping board running full .Net Standard 2.X
  Toggle Switch spst: Toggle Switch single pole single throw
