# Fritzing sketch AnalogTemperature (saved by Fritzing 0.9.3b)
breadboards: 1

parts:
  Meadow1 = Meadow F7
  T1 = TMP36 Temperature Sensor [package="TO92 [THT]"]

nets:
  GND: Meadow1.GND, T1.GND
  N1: Meadow1.3V3, T1.+Vs
  N2: Meadow1.A0, T1.Vout

custom parts:
  Meadow F7: A prototyping board running full .Net Standard 2.X
