# Fritzing sketch Servo (saved by Fritzing 0.9.3b)
breadboards: 1

parts:
  Meadow1 = Meadow F7
  M1 = Dagu DGServo 9g (Top view) [part_number=RS001B]
  VCC1 = 4 x AAA Battery Mount

nets:
  GND: Meadow1.GND, M1.gnd, VCC1.-
  N1: Meadow1.D12, M1.pulse
  N2: M1.vcc, VCC1.+

custom parts:
  Meadow F7: A prototyping board running full .Net Standard 2.X
