# Fritzing sketch PiezoSpeaker (saved by Fritzing 0.9.3b)
breadboards: 1

parts:
  Meadow1 = Meadow F7
  J1 = Piezo Speaker

nets:
  N1: Meadow1.GND, J1.pin1
  N2: Meadow1.D10, J1.pin2

custom parts:
  Meadow F7: A prototyping board running full .Net Standard 2.X
