# Fritzing sketch CharacterDisplay (saved by Fritzing 0.9.3b)
breadboards: 1

parts:
  Meadow1 = Meadow F7
  LCD1 = LCD screen
  R1 = Rotary Potentiometer (Small) [maximum_resistance=10kΩ package=THT]

nets:
  GND: Meadow1.GND, LCD1.VSS, LCD1.R/W, LCD1.LED-, R1.leg1
  N1: Meadow1.D11, LCD1.DB7
  N2: Meadow1.D10, LCD1.DB6
  N3: Meadow1.D09, LCD1.DB5
  N4: Meadow1.SCK/D08, LCD1.DB4
  N5: Meadow1.SDA/D07, LCD1.E
  N6: Meadow1.D05, LCD1.RS
  +5V: Meadow1.+5V, LCD1.VDD, LCD1.LED+, R1.leg2
  N7: LCD1.V0, R1.wiper

custom parts:
  Meadow F7: A prototyping board running full .Net Standard 2.X
