# Fritzing sketch Mcp23x08_Fritzing (saved by Fritzing 0.9.3b)
breadboards: 1

parts:
  Meadow2 = Meadow F7
  R11 = Resistor [tolerance=±5% resistance=220 package=THT]
  R12 = Resistor [tolerance=±5% resistance=220 package=THT]
  R13 = Resistor [tolerance=±5% resistance=220 package=THT]
  R14 = Resistor [tolerance=±5% resistance=220 package=THT]
  R15 = Resistor [tolerance=±5% resistance=220 package=THT]
  R16 = Resistor [tolerance=±5% resistance=220 package=THT]
  R17 = Resistor [tolerance=±5% resistance=220 package=THT]
  R18 = Resistor [tolerance=±5% resistance=220 package=THT]
  LED10 = LED - 5mm [color="Red (633nm)" package="5 mm [THT]"]
  LED11 = LED - 5mm [color="Red (633nm)" package="5 mm [THT]"]
  LED12 = LED - 5mm [color="Red (633nm)" package="5 mm [THT]"]
  LED13 = LED - 5mm [color="Red (633nm)" package="5 mm [THT]"]
  LED14 = LED - 5mm [color="Red (633nm)" package="5 mm [THT]"]
  LED15 = LED - 5mm [color="Red (633nm)" package="5 mm [THT]"]
  LED16 = LED - 5mm [color="Red (633nm)" package="5 mm [THT]"]
  LED17 = LED - 5mm [color="Red (633nm)" package="5 mm [THT]"]
  R19 = Resistor [tolerance=±5% resistance=4.1k package=THT]
  R20 = Resistor [tolerance=±5% resistance=4.1k package=THT]
  IC6 = FRM010 [package=THT]

nets:
  N1: Meadow2.GND, R11.Pin_1, R12.Pin_1, R13.Pin_1, R14.Pin_1, R15.Pin_1, R16.Pin_1, R17.Pin_1, R18.Pin_1, IC6.LCD_D7, IC6.LCD_PWR
  N2: Meadow2.SCK/D08, R19.Pin_0, IC6.JP1_-_Welcome_Message_selection
  N3: Meadow2.SDA/D07, R20.Pin_0, IC6.JP2_-_Baud_Rate_selection
  N4: Meadow2.3V3, R19.Pin_1, R20.Pin_1, IC6.JP3_-_Polarity_selection, IC6.JP4_-_Number_of_Lines_selection, IC6.+V, IC6.XTAL#14
  N5: R11.Pin_0, LED17.cathode
  N6: R12.Pin_0, LED11.cathode
  N7: R13.Pin_0, LED12.cathode
  N8: R14.Pin_0, LED13.cathode
  N9: R15.Pin_0, LED10.cathode
  N10: R16.Pin_0, LED14.cathode
  N11: R17.Pin_0, LED15.cathode
  N12: R18.Pin_0, LED16.cathode
  N13: LED10.anode, IC6.LCD_RS
  N14: LED11.anode, IC6.LCD_E
  N15: LED12.anode, IC6.Serial_In
  N16: LED13.anode, IC6.Reset
  N17: LED14.anode, IC6.0V
  N18: LED15.anode, IC6.LCD_D4
  N19: LED16.anode, IC6.LCD_D5
  N20: LED17.anode, IC6.LCD_D6

custom parts:
  Meadow F7: A prototyping board running full .Net Standard 2.X
