# Fritzing sketch HBridgeMotor (saved by Fritzing 0.9.3b)
breadboards: 1

parts:
  Meadow1 = Meadow F7
  IC1 = H-Bridge [package=THT]
  M1 = DC Motor
  M2 = DC Motor
  VCC1 = 4 x AAA Battery Mount

nets:
  N1: Meadow1.D13, IC1.3_4EN
  N2: Meadow1.D12, IC1.3A
  N3: Meadow1.D10, IC1.1_2EN
  N4: Meadow1.D09, IC1.1A
  N5: Meadow1.SCK/D08, IC1.2A
  N6: Meadow1.D14, IC1.4A
  N7: IC1.1Y, M2.pin_2
  GND1: IC1.GND1, IC1.GND2, IC1.GND3, IC1.GND4, VCC1.-
  N8: IC1.2Y, M2.pin_1
  N9: IC1.VCC2, IC1.VCC1, VCC1.+
  N10: IC1.3Y, M1.pin_2
  N11: IC1.4Y, M1.pin_1

custom parts:
  Meadow F7: A prototyping board running full .Net Standard 2.X
