# Fritzing sketch HCSR04 (saved by Fritzing 0.9.3b)
breadboards: 1

parts:
  Meadow1 = Meadow F7
  HC-SR04_Sensor_1 = HC-SR04 Ultrasonic Distance Sensor

nets:
  GND: Meadow1.GND, HC-SR04_Sensor_1.GND
  N1: Meadow1.D13, HC-SR04_Sensor_1.ECHO
  3V3: Meadow1.3V3, HC-SR04_Sensor_1.VCC
  N2: Meadow1.D14, HC-SR04_Sensor_1.TRIG

custom parts:
  Meadow F7: A prototyping board running full .Net Standard 2.X
