# Fritzing sketch FC28 (saved by Fritzing 0.9.3b)
breadboards: 1

parts:
  Meadow1 = Meadow F7
  Part1 = FC-28 Soil Hygrometer Module
  Part2 = FC-28 Soil Hygrometer Module - Probe

nets:
  GND: Meadow1.GND, Part1.GND
  N1: Meadow1.D14, Part1.VCC
  N2: Meadow1.A0, Part1.AO
  N3: Part1.POS, Part2.POS
  N4: Part1.NEG, Part2.NEG

custom parts:
  Meadow F7: A prototyping board running full .Net Standard 2.X
  FC-28 Soil Hygrometer Module: The FC-28 is a soil hygrometer module that uses the Texas Instruments LM393 comparator chip to provide an analog measurement of soil humidity. The digital output is high when soil moisture is over a certain threshold, as determined by adjusting the potentiometer.
  FC-28 Soil Hygrometer Module - Probe: The FC-28 is a soil hygrometer module that uses the Texas Instruments LM393 comparator chip to provide an analog measurement of soil humidity.
