# Fritzing sketch Adxl345c (saved by Fritzing 0.9.3b)
breadboards: 1

parts:
  Part2 = Triple Axis Accelerometer Breakout - ADXL345
  R3 = Resistor [tolerance=±5% resistance=4.7k package=THT]
  R4 = Resistor [tolerance=±5% resistance=4.7k package=THT]
  Meadow1 = Meadow F7

nets:
  GND: Part2.GND, Part2.SDO, Meadow1.GND
  VCC: Part2.VCC, Part2.CS, R3.Pin_1, R4.Pin_1, Meadow1.3V3
  N1: Part2.SDA, R3.Pin_0, Meadow1.SDA/D07
  N2: Part2.SCL, R4.Pin_0, Meadow1.SCK/D08

custom parts:
  Meadow F7: A prototyping board running full .Net Standard 2.X
