# Fritzing sketch IDxxLA-RFID USB Reader (saved by Fritzing 0.9.4)
breadboards: 1

parts:
  Mod1 = Meadow F7 Micro
  Part1 = RFID USB Reader

nets:
  GND: Mod1.GND, Part1.GNDT, Part1.GND
  N1: Mod1.D13, Part1.TX-O
  +5V: Mod1.+5V, Part1.VCC
