# Fritzing sketch DipSwitch (saved by Fritzing 0.9.3b)
breadboards: 1

parts:
  SW1 = DIP Switch 8 Position [package=dipswitch-08]
  Meadow1 = Meadow F7

nets:
  N1: SW1.1, Meadow1.D12
  N2: SW1.2, Meadow1.D11
  N3: SW1.3, Meadow1.D10
  N4: SW1.4, Meadow1.D09
  N5: SW1.5, Meadow1.SCK/D08
  N6: SW1.6, Meadow1.SDA/D07
  N7: SW1.7, Meadow1.D06
  N8: SW1.8, Meadow1.D05
  N9: SW1.9, SW1.10, SW1.11, SW1.12, SW1.13, SW1.14, SW1.15, SW1.16, Meadow1.GND

custom parts:
  Meadow F7: A prototyping board running full .Net Standard 2.X
