# Fritzing sketch SpdtSwitch (saved by Fritzing 0.9.3b)
breadboards: 1

parts:
  Meadow1 = Meadow F7
  S1 = Toggle Switch [package=THT]

nets:
  N1: Meadow1.GND, S1.L1
  N2: Meadow1.D13, S1.COM
  N3: Meadow1.3V3, S1.L2

custom parts:
  Meadow F7: A prototyping board running full .Net Standard 2.X
