# Fritzing sketch DS18B20 (saved by Fritzing 0.9.3b)
breadboards: 1

parts:
  Meadow1 = Meadow F7
  DS2 = DS18B20 1-Wire Temperature Sensor [part_number=DS18B20]
  R2 = Resistor [tolerance=±5% resistance=4.7k package=THT]

nets:
  GND: Meadow1.GND, DS2.GND, R2.Pin_0
  N1: Meadow1.D09, DS2.DQ, R2.Pin_1
  3V3: Meadow1.3V3, DS2.VDD

custom parts:
  Meadow F7: A prototyping board running full .Net Standard 2.X
