# Fritzing sketch TMP102 (saved by Fritzing 0.9.3b)
breadboards: 1

parts:
  Part1 = Digital Temperature Sensor Breakout - TMP102
  Meadow1 = Meadow F7

nets:
  N1: Part1.V+, Meadow1.3V3
  N2: Part1.SDA, Meadow1.SDA/D07
  N3: Part1.SCL, Meadow1.SCK/D08
  GND: Part1.GND, Meadow1.GND

custom parts:
  Meadow F7: A prototyping board running full .Net Standard 2.X
