# Fritzing sketch LED_Circuit (saved by Fritzing 0.9.3b)
breadboards: 1

parts:
  Netduino1 = Netduino Plus2
  LED1 = LED - 5mm [color="Red (633nm)" package="5 mm [THT]"]
  R1 = Resistor [tolerance=±5% resistance=160k package=THT]

nets:
  N1: Netduino1.D9_PWM2, R1.Pin_0
  N2: Netduino1.GND, LED1.cathode
  N3: LED1.anode, R1.Pin_1
