# Fritzing sketch Keyes_Relay (saved by Fritzing 0.9.3b)
breadboards: 1

parts:
  5V_Relay_Power = DC Power [voltage=5]
  Netduino = Netduino Plus2
  5V_Relay_Power1 = DC Power [voltage=5]
  Relay_Header = Header 6 [package=1x06_smd_straight_alt]

nets:
  N1: 5V_Relay_Power.V+, Relay_Header.1
  N2: 5V_Relay_Power.V-, Relay_Header.2
  GND: Netduino.GND, 5V_Relay_Power1.V-, Relay_Header.5
  N3: Netduino.D3_TX1, Relay_Header.3
  N4: Netduino.D2_RX1, Relay_Header.4
  N5: Netduino.VIN, 5V_Relay_Power1.V+

notes:
  Relay Header
  5V Relay Power
