# Fritzing sketch Parallel_Resistance_Lab (saved by Fritzing 0.9.3b)
breadboards: 1

parts:
  R1 = Resistor [tolerance=±5% resistance=330 package=THT]
  R2 = Resistor [tolerance=±5% resistance=1k package=THT]
  R5 = Resistor [tolerance=±5% resistance=330 package=THT]
  R6 = Resistor [tolerance=±5% resistance=1k package=THT]

nets:
  N1: R1.Pin_0, R2.Pin_0
  N2: R1.Pin_1, R2.Pin_1
  N3: R5.Pin_0, R6.Pin_0
  N4: R5.Pin_1, R6.Pin_1

notes:
  Place probe 1 here.
  Place probe 2 here.
  Sample Configuration 1
  Sample Configuration 2
