# Fritzing sketch Level_Shifting_Lab_Divider_Validation (saved by Fritzing 0.9.3b)
breadboards: 1

parts:
  Netduino = Netduino Plus2
  R1 = Resistor [tolerance=±5% resistance=1k package=THT]
  R2 = Resistor [tolerance=±5% resistance=2.2k package=THT]

nets:
  N1: Netduino.+5V, R1.Pin_0
  N2: Netduino.GND, R2.Pin_1
  N3: Netduino.A2, R1.Pin_1, R2.Pin_0
