# Fritzing sketch Photoresistor_Circuit (saved by Fritzing 0.9.3b)
breadboards: 1

parts:
  R1 = Resistor [tolerance=±5% resistance=4.7k package=THT]
  R2 = PHOTOCELL [package=photocell]
  Netduino = Netduino Plus2

nets:
  N1: R1.Pin_0, Netduino.3V3
  N2: R1.Pin_1, R2.P$1, Netduino.A3
  N3: R2.P$2, Netduino.GND
