# Fritzing sketch RGB_Blinky (saved by Fritzing 0.9.3b)
breadboards: 1

parts:
  Netduino1 = Netduino Plus2
  RGB_LED_(Common_Anode) = RGB LED - (4 legs) [package="5 mm [THT]"]
  R1 = Resistor [tolerance=±5% resistance=4.7 package=THT]
  R2 = Resistor [tolerance=±5% resistance=4.7 package=THT]
  R3 = Resistor [tolerance=±5% resistance=47 package=THT]

nets:
  N1: Netduino1.D5_PWM0, R2.Pin_0
  N2: Netduino1.D4_CS0, R1.Pin_0
  N3: Netduino1.D3_TX1, R3.Pin_0
  N4: Netduino1.3V3, RGB_LED_(Common_Anode).common_anode
  N5: RGB_LED_(Common_Anode).red_cathode, R3.Pin_1
  N6: RGB_LED_(Common_Anode).green_cathode, R1.Pin_1
  N7: RGB_LED_(Common_Anode).blue_cathode, R2.Pin_1
